# Fritzing sketch circuito (saved by Fritzing 0.6.3b)
breadboards: 2

parts:
  IC1 = H-Bridge [package=THT]
  Arduino1 = Arduino
  Power_plug1 = Power plug
  M1 = DC Motor
  S1 = Toggle Switch [package=THT]
  R1 = Rotary Potentiometer (Small) [maximum_resistance=100kΩ]
  R2 = Resistor [tolerance=±5% resistance=220 package=THT]
  M2 = DC Motor
  IC2 = H-Bridge [package=THT]
  Power_plug2 = Power plug
  M3 = DC Motor
  R3 = Rotary Potentiometer (Small) [maximum_resistance=100kΩ]
  M4 = DC Motor
  Arduino2 = Arduino

nets:
  N1: IC1.1_2EN, Arduino1.D9
  N2: IC1.1A, Arduino1.D3
  N3: IC1.1Y, M1.pin_1
  GND: IC1.GND1, IC1.GND2, IC1.GND3, IC1.GND4, Arduino1.GND, Power_plug1.GND, R1.leg1, R2.Pin_0
  N4: IC1.2Y, M1.pin_2
  N5: IC1.2A, Arduino1.D4
  N6: IC1.VCC2, Power_plug1.VCC
  N7: IC1.3_4EN, Arduino1.D10
  N8: IC1.3A, Arduino1.D5
  N9: IC1.3Y, M2.pin_2
  N10: IC1.4Y, M2.pin_1
  N11: IC1.4A, Arduino1.D6
  N12: IC1.VCC1, Arduino1.+5V, S1.L1, R1.leg2
  N13: Arduino1.D2, S1.COM, R2.Pin_1
  N14: Arduino1.A0, R1.wiper
  N15: IC2.1_2EN, Arduino2.D9
  N16: IC2.1A, Arduino2.D3
  N17: IC2.1Y, M3.pin_1
  GND_2: IC2.GND1, IC2.GND2, IC2.GND3, IC2.GND4, Power_plug2.GND, R3.leg1, Arduino2.GND
  N18: IC2.2Y, M3.pin_2
  N19: IC2.2A, Arduino2.D4
  N20: IC2.VCC2, Power_plug2.VCC
  N21: IC2.3_4EN, Arduino2.D10
  N22: IC2.3A, Arduino2.D5
  N23: IC2.3Y, M4.pin_2
  N24: IC2.4Y, M4.pin_1
  N25: IC2.4A, Arduino2.D6
  N26: IC2.VCC1, R3.leg2, Arduino2.+5V
  N27: R3.wiper, Arduino2.A0
